// Digital circuit 2_to_4_decode_w_enable.dig as structural Verilog
module _2_to_4_decode_w_enable (
  input  [3:0] Sel,
  input  EN,
  output out0,
  output out1,
  output out2,
  output out3,
  output out4,
  output out5,
  output out6,
  output out7,
  output out8,
  output out9,
  output out10,
  output out11,
  output out12,
  output out13,
  output out14,
  output out15
);

  wire decoder_1_out_0, decoder_1_out_1, decoder_1_out_2, decoder_1_out_3, decoder_1_out_4, decoder_1_out_5,
       decoder_1_out_6, decoder_1_out_7, decoder_1_out_8, decoder_1_out_9, decoder_1_out_10,
       decoder_1_out_11, decoder_1_out_12, decoder_1_out_13, decoder_1_out_14, decoder_1_out_15;

  Decoder #(.Selector_Bits(4)) decoder_1 (
    .sel(Sel), .out_0(decoder_1_out_0), .out_1(decoder_1_out_1), .out_2(decoder_1_out_2),
    .out_3(decoder_1_out_3), .out_4(decoder_1_out_4), .out_5(decoder_1_out_5), .out_6(decoder_1_out_6),
    .out_7(decoder_1_out_7), .out_8(decoder_1_out_8), .out_9(decoder_1_out_9), .out_10(decoder_1_out_10),
    .out_11(decoder_1_out_11), .out_12(decoder_1_out_12), .out_13(decoder_1_out_13),
    .out_14(decoder_1_out_14), .out_15(decoder_1_out_15));
  and and_1 (out0, decoder_1_out_0, EN);
  and and_2 (out1, decoder_1_out_1, EN);
  and and_3 (out2, decoder_1_out_2, EN);
  and and_4 (out3, decoder_1_out_3, EN);
  and and_5 (out4, decoder_1_out_4, EN);
  and and_6 (out5, decoder_1_out_5, EN);
  and and_7 (out6, decoder_1_out_6, EN);
  and and_8 (out7, decoder_1_out_7, EN);
  and and_9 (out8, decoder_1_out_8, EN);
  and and_10 (out9, decoder_1_out_9, EN);
  and and_11 (out10, decoder_1_out_10, EN);
  and and_12 (out11, decoder_1_out_11, EN);
  and and_13 (out12, decoder_1_out_12, EN);
  and and_14 (out13, decoder_1_out_13, EN);
  and and_15 (out14, decoder_1_out_14, EN);
  and and_16 (out15, decoder_1_out_15, EN);
endmodule
