// Digital circuit ALU.dig as structural Verilog
module ALU (
  input  [31:0] A,
  input  [31:0] B,
  input  [1:0] ALUop,
  output [31:0] R,
  output [3:0] NZCV,
  output N,
  output Z,
  output C,
  output V
);

  wire and_1_out, and_2_out;
  wire [30:0] sub_1_s;
  wire [31:0] add_1_s;
  wire [63:0] mul_1_mul;

  Comparator #(.Bits(32)) comparator_1 (.a({N, sub_1_s}), .b({32{1'b0}}), .eq(NZCV[1]));  // open: gt, lt
  Comparator #(.Bits(32)) comparator_2 (.a(A), .b(B), .gt(C));  // open: eq, lt
  and and_1 (and_1_out, ~A[31], B[31], N);  // And
  and and_2 (and_2_out, A[31], ~B[31], ~N);  // And
  Add #(.Bits(32)) add_1 (.a(A), .b(B), .c_i(1'b0), .s(add_1_s));  // open: c_o
  Sub #(.Bits(32)) sub_1 (.a(A), .b(B), .c_i(1'b0), .s({N, sub_1_s}));  // open: c_o
  Mul #(.Bits(32)) mul_1 (.a(A), .b(B), .mul(mul_1_mul));
  or or_1 (NZCV[3], and_1_out, and_2_out);
  Multiplexer #(.Selector_Bits(2), .Bits(32)) multiplexer_1 (
    .sel(ALUop), .in_0(add_1_s), .in_1({N, sub_1_s}), .in_2(mul_1_mul[31:0]), .in_3(B), .out(R));

  assign {NZCV[2], NZCV[0]} = {C, N};
  assign V = NZCV[3];
  assign Z = NZCV[1];

  // Other names for the same wires on the sheet: r31 = N
endmodule
