// Digital circuit ROM_programs.dig as structural Verilog
module ROM_programs (
  input  [4:0] A,
  input  [3:0] PN,
  output [31:0] D
);

  wire [31:0] fib_iter_10_d, fib_iter_19_d, fib_rec_10_d, fib_rec_19_d, find_max1_d, find_max2_d,
       quadratic_1_d, quadratic_2_d, sum_1_d, sum_2_d, sum_test_d;

  ROM #(.AddrBits(5), .Bits(32)) quadratic_1 (.A(A), .sel(1'b1), .D(quadratic_1_d));
  ROM #(.AddrBits(5), .Bits(32)) quadratic_2 (.A(A), .sel(1'b1), .D(quadratic_2_d));
  ROM #(.AddrBits(5), .Bits(32)) sum_1 (.A(A), .sel(1'b1), .D(sum_1_d));
  ROM #(.AddrBits(5), .Bits(32)) sum_2 (.A(A), .sel(1'b1), .D(sum_2_d));
  ROM #(.AddrBits(5), .Bits(32)) find_max1 (.A(A), .sel(1'b1), .D(find_max1_d));
  ROM #(.AddrBits(5), .Bits(32)) find_max2 (.A(A), .sel(1'b1), .D(find_max2_d));
  ROM #(.AddrBits(5), .Bits(32)) fib_iter_10 (.A(A), .sel(1'b1), .D(fib_iter_10_d));
  ROM #(.AddrBits(5), .Bits(32)) fib_iter_19 (.A(A), .sel(1'b1), .D(fib_iter_19_d));
  ROM #(.AddrBits(5), .Bits(32)) fib_rec_10 (.A(A), .sel(1'b1), .D(fib_rec_10_d));
  ROM #(.AddrBits(5), .Bits(32)) fib_rec_19 (.A(A), .sel(1'b1), .D(fib_rec_19_d));
  ROM #(.AddrBits(5), .Bits(32)) sum_test (.A(A), .sel(1'b1), .D(sum_test_d));
  Multiplexer #(.Selector_Bits(4), .Bits(32)) multiplexer_1 (
    .sel(PN), .in_0(quadratic_1_d), .in_1(quadratic_2_d), .in_2(sum_1_d), .in_3(sum_2_d), .in_4(find_max1_d),
    .in_5(find_max2_d), .in_6(fib_iter_10_d), .in_7(fib_iter_19_d), .in_8(fib_rec_10_d), .in_9(fib_rec_19_d),
    .in_10(sum_test_d), .in_11({32{1'b0}}), .in_12({32{1'b0}}), .in_13({32{1'b0}}), .in_14({32{1'b0}}),
    .in_15({32{1'b0}}), .out(D));

  // Notes on the sheet:
  //   r0: 7
  //   r1: 0
  //   r2: 4
  //   r3: -1
  //   Expected result = 27
  //   Array: [1, 2, 3, 4, 5]
  //   Expected result = 15
  //   Array: [-4, -9, 8, 22, 2]
  //   Expected result = 19
  //   Array: [5, 7, 2, 1, 9]
  //   Expected result = 9
  //   Array: [0, -5, 0, 3, 1]
  //   Expected result = 3
  //   fib_iter(10) = 55
  //   fib_iter(19) = 4181
  //   fib_rec(10) = 55
  //   fib_rec(19) = 4181
  //   contents of quadratic_1 (hex, n*v repeats v):
  //   e3a0d080,e24dd00c,e3a00001,e58d0000,e3a00002,e58d0004,e3a00003,e58d0008,e1a0000d,
  //   e3a01003,eb000000,eafffffe,e3a02000,e3a03000,e1520001,a000004,e590c000,e083300c,e2822001,
  //   e2800004,eafffff8,e1a00003,e12fff1e
  //   contents of quadratic_2 (hex, n*v repeats v):
  //   e3a00007,e3a01000,e3a02004,e3a03000,e2433001,eb000000,eafffffe,e0020290,e0010190,
  //   e0010190,e0833001,e0833002,e1a00003,e12fff1e
  //   contents of sum_1 (hex, n*v repeats v):
  //   e3a0d080,e24dd014,e3a00001,e58d0000,e3a00002,e58d0004,e3a00003,e58d0008,e3a00004,
  //   e58d000c,e3a00005,e58d0010,e1a0000d,e3a01005,eb000000,eafffffe,e3a02000,e3a03000,
  //   e1520001,a000004,e590c000,e083300c,e2822001,e2800004,eafffff8,e1a00003,e12fff1e
  //   contents of sum_2 (hex, n*v repeats v):
  //   e3a0d080,e24dd014,e3a00000,e2400004,e58d0000,e3a00000,e2400009,e58d0004,e3a00008,
  //   e58d0008,e3a00016,e58d000c,e3a00002,e58d0010,e1a0000d,e3a01005,eb000000,eafffffe,
  //   e3a02000,e3a03000,e1520001,a000004,e590c000,e083300c,e2822001,e2800004,eafffff8,e1a00003,
  //   e12fff1e
  //   contents of find_max1 (hex, n*v repeats v):
  //   e3a0d080,e24dd014,e3a00005,e58d0000,e3a00007,e58d0004,e3a00002,e58d0008,e3a00001,
  //   e58d000c,e3a00009,e58d0010,e1a0000d,e3a01005,eb000000,eafffffe,e3a02000,e590c000,
  //   e1a0300c,e1520001,a000006,e2800004,e590c000,e15c0003,ba000000,e1a0300c,e2822001,eafffff6,
  //   e1a00003,e12fff1e
  //   contents of find_max2 (hex, n*v repeats v):
  //   e3a0d080,e24dd014,e3a00000,e58d0000,e3a00000,e2400005,e58d0004,e3a00000,e58d0008,
  //   e3a00003,e58d000c,e3a00001,e58d0010,e1a0000d,e3a01005,eb000000,eafffffe,e3a02000,
  //   e590c000,e1a0300c,e1520001,a000006,e2800004,e590c000,e15c0003,ba000000,e1a0300c,e2822001,
  //   eafffff6,e1a00003,e12fff1e
  //   contents of fib_iter_10 (hex, n*v repeats v):
  //   e3a0000a,eb000000,eafffffe,e3500000,a00000c,e3a01000,e3a02000,e3a03001,e3a0c001,e150000c,
  //   a000004,e1a01002,e1a02003,e0823001,e28cc001,eafffff8,e1a00003,e12fff1e,e12fff1e
  //   contents of fib_iter_19 (hex, n*v repeats v):
  //   e3a00013,eb000000,eafffffe,e3500000,a00000c,e3a01000,e3a02000,e3a03001,e3a0c001,e150000c,
  //   a000004,e1a01002,e1a02003,e0823001,e28cc001,eafffff8,e1a00003,e12fff1e,e12fff1e
  //   contents of fib_rec_10 (hex, n*v repeats v):
  //   e3a0000a,e3a0d080,eb000000,eafffffe,e24dd010,e3500001,ca000000,ea00000b,e58de000,
  //   e58d0004,e2400001,ebfffff7,e58d0008,e59d0004,e2400002,ebfffff3,e1a01000,e59d0008,
  //   e0800001,e59de000,e28dd010,e12fff1e
  //   contents of fib_rec_19 (hex, n*v repeats v):
  //   e3a00013,e3a0d080,eb000000,eafffffe,e24dd010,e3500001,ca000000,ea00000b,e58de000,
  //   e58d0004,e2400001,ebfffff7,e58d0008,e59d0004,e2400002,ebfffff3,e1a01000,e59d0008,
  //   e0800001,e59de000,e28dd010,e12fff1e
  //   contents of sum_test (hex, n*v repeats v):
  //   e3a0d080,e24dd00c,e3a00001,e58d0000,e3a00002,e58d0004,e3a00003,e58d0008,e1a0000d,
  //   e3a01003,eb000000,eafffffe,e3a02000,e3a03000,e1520001,a000004,e590c000,e083300c,e2822001,
  //   e2800004,eafffff8,e1a00003,e12fff1e
  //   r0: 2
  //   r1: 3
  //   r2: 4
  //   r3: 5
  //   Expected result = 25
endmodule
