// Digital circuit main_decoder.dig as structural Verilog
module main_decoder (
  input  [31:0] iw,
  output RFW,
  output [1:0] EXT,
  output BR,
  output ALU1src,
  output BL,
  output BX,
  output [1:0] ALUop,
  output MemWrite,
  output MemToReg,
  output cmp
);

  wire add_i, add_r, comparator_1_eq, comparator_2_eq, comparator_3_eq, comparator_5_eq, comparator_6_eq,
       comparator_7_eq, comparator_8_eq, comparator_9_eq, comparator_10_eq, ldr_i, ldr_r, mov_i, mov_r, mul,
       or_1_out, or_2_out, or_3_out, or_4_out, or_5_out, or_6_out, str_i, str_r, sub_i, sub_r;

  // Probe on iw
  Comparator #(.Bits(4)) comparator_1 (.a(iw[24:21]), .b(4'b0100), .eq(comparator_1_eq));  // open: gt, lt
  Comparator #(.Bits(4)) comparator_2 (.a(iw[24:21]), .b(4'b0010), .eq(comparator_2_eq));  // open: gt, lt
  Comparator #(.Bits(4)) comparator_3 (.a(iw[24:21]), .b(4'b1101), .eq(comparator_3_eq));  // open: gt, lt
  Comparator #(.Bits(4)) comparator_4 (.a(iw[24:21]), .b(4'b1010), .eq(cmp));  // open: gt, lt
  and and_1 (add_r, ~iw[27], ~iw[26], ~iw[25], comparator_1_eq);  // And
  and and_2 (add_i, ~iw[27], ~iw[26], iw[25], comparator_1_eq);  // And
  and and_3 (sub_r, ~iw[27], ~iw[26], ~iw[25], comparator_2_eq);  // And
  and and_4 (sub_i, ~iw[27], ~iw[26], iw[25], comparator_2_eq);  // And
  and and_5 (mov_r, ~iw[27], ~iw[26], ~iw[25], comparator_3_eq);  // And
  and and_6 (mov_i, ~iw[27], ~iw[26], iw[25], comparator_3_eq);  // And
  Comparator #(.Bits(4)) comparator_5 (.a(iw[7:4]), .b(4'b1001), .eq(comparator_5_eq));  // open: gt, lt
  Comparator #(.Bits(6)) comparator_6 (.a(iw[27:22]), .b({6{1'b0}}), .eq(comparator_6_eq));  // open: gt, lt
  Comparator #(.Bits(2)) comparator_7 (.a(iw[27:26]), .b(2'b01), .eq(comparator_7_eq));  // open: gt, lt
  Comparator #(.Bits(2)) comparator_8 (.a(iw[27:26]), .b(2'b01), .eq(comparator_8_eq));  // open: gt, lt
  Comparator #(.Bits(2)) comparator_9 (.a(iw[27:26]), .b(2'b01), .eq(comparator_9_eq));  // open: gt, lt
  Comparator #(.Bits(2)) comparator_10 (.a(iw[27:26]), .b(2'b01), .eq(comparator_10_eq));  // open: gt, lt
  and and_7 (mul, comparator_5_eq, comparator_6_eq);
  and and_8 (ldr_r, iw[20], iw[25], comparator_7_eq);
  and and_9 (ldr_i, iw[20], ~iw[25], comparator_8_eq);  // And
  and and_10 (str_r, ~iw[20], iw[25], comparator_9_eq);  // And
  and and_11 (str_i, ~iw[20], ~iw[25], comparator_10_eq);  // And
  and and_12 (BR, iw[27], ~iw[26], iw[25]);  // And
  and and_13 (BL, BR, iw[24]);
  Comparator #(.Bits(24)) comparator_11 (.a(iw[27:4]), .b(24'h12fff1), .eq(BX));  // open: gt, lt
  or or_1 (or_1_out, sub_r, sub_i);
  or or_2 (or_2_out, mov_r, mov_i);
  or or_3 (or_3_out, add_i, mov_i, ldr_i, BR, sub_i);
  or or_4 (or_4_out, iw[25], str_i);
  or or_5 (or_5_out, add_r, add_i, sub_r, sub_i, mov_i);
  or or_6 (or_6_out, mov_r, mul, BL, ldr_i, ldr_r);
  or or_7 (RFW, or_5_out, or_6_out);
  or or_8 (EXT[0], ldr_i, str_i);
  or or_9 (EXT[1], BR, 1'b0);
  or or_10 (ALU1src, or_3_out, or_4_out);
  or or_11 (ALUop[0], or_1_out, or_2_out);
  or or_12 (ALUop[1], mul, or_2_out);
  or or_13 (MemToReg, ldr_r, ldr_i);
  or or_14 (MemWrite, str_r, str_i);

  // Other names for the same wires on the sheet: b_offset[23:0] = iw[23:0]; imm[7:0] = iw[7:0];
  //   immoff[11:0] = iw[11:0]; rm[3:0] = iw[3:0]; rm_mul[3:0] = iw[3:0]; opmul4[3:0] = iw[7:4];
  //   rs_mul[3:0] = iw[11:8]; rd[3:0] = iw[15:12]; rn_mul[3:0] = iw[15:12]; rd_mul[3:0] = iw[19:16];
  //   rn[3:0] = iw[19:16]; l_sdt = iw[20]; s_dp = iw[20]; s_mul = iw[20]; a_mul = iw[21]; opc[3:0] = iw[24:21];
  //   w_sdt = iw[21]; b_sdt = iw[22]; opmul6[5:0] = iw[27:22]; u_sdt = iw[23]; l_b = iw[24]; p_sdt = iw[24];
  //   cmp_i = iw[25]; i_dp = iw[25]; i_sdt = iw[25]; op0 = iw[25]; op1 = iw[26]; opmul2[1:0] = iw[27:26];
  //   op2 = iw[27]; cond[3:0] = iw[31:28]

  // Notes on the sheet:
  //   sub(r) (subtraction with registers)
  //   sub(i) (subtraction with an immediate val)
  //   add(r) (adding with registers)
  //   add(i) (adding with an immediate value)
  //   mov(r), move with a register
  //   mov(i), move with an immediate value
  //   Multiply
  //   str with an immediate value
  //   ldr with registers
  //   ldr with an immediate value
  //   str with registers
  //   br (Branch)
  //   bl (branch and link)
  //   bx (branch and exchange)
  //   (Register write file)
  //   00 - 8-bit zero extension
  //   01 - 12-bit zero extension
  //   10 - 24-bit sign extension
  //   (Extend Immediate value)
  //   00 - add
  //   01 - sub
  //   10 - mul
  //   11- mov
  //   imm or not?
  //   Branch (b)
  //   Branch and Link
  //   Branch and Exchange
endmodule
