// Digital circuit processor_main.dig as structural Verilog
module processor_main (
  input  CLK,
  output [31:0] out_2
);

  wire a_mul, ALU1src, and_1_out, BL, BR, BX, C, comparator_1_eq, dipswitch_1_out, i_dp, MemToReg, MemWrite,
       N, RFW, V, Z;
  wire [1:0] ALUop, EXT;
  wire [3:0] cond, multiplexer_4_out, multiplexer_5_out, multiplexer_6_out, multiplexer_7_out,
       multiplexer_8_out, multiplexer_9_out, NZCV;
  wire [8:0] alu_1_p4;
  wire [23:0] b_offset;
  wire [27:24] iw;
  wire [31:0] add_1_s, add_2_s, extension_unit_1_extimm, multiplexer_1_out, multiplexer_3_out,
       multiplexer_10_out, pc_in, pc_out, r0, r1, r2, r3, r4, r5, r6, r7, r8, r9, r10, r11, r12, r13, r14,
       r15, ramdualport_1_d, register_file_1_rd0, register_file_1_rd1;
  wire [31:9] alu_1_p4_2;

  and and_1 (and_1_out, CLK, dipswitch_1_out);
  DipSwitch dipswitch_1 (.out(dipswitch_1_out));
  Multiplexer #(.Bits(32)) multiplexer_1 (.sel(BR), .in_0(add_1_s), .in_1(out_2), .out(multiplexer_1_out));
  Multiplexer #(.Bits(32)) multiplexer_2 (.sel(BX), .in_0(multiplexer_1_out), .in_1(register_file_1_rd1), .out(pc_in));
  // Probe on pc_in
  Register #(.Bits(32)) PC (.D(pc_in), .C(and_1_out), .en(1'b1), .Q(pc_out));
  control_unit control_unit_1 (
    .iw({cond, iw[27:26], i_dp, iw[24], b_offset[23:22], a_mul, b_offset[20:0]}), .NZCV(NZCV),
    .CLK(and_1_out), .RFW(RFW), .EXT(EXT), .ALUop(ALUop), .ALU1src(ALU1src), .BR(BR), .BL(BL), .BX(BX),
    .MemToReg(MemToReg), .MemWrite(MemWrite));
  // Probe on NZCV
  // Probe on pc_out
  Add #(.Bits(32)) add_1 (.a(pc_out), .b(32'h4), .c_i(1'b0), .s(add_1_s));  // open: c_o
  ROM_programs rom_programs_1 (
    .A(pc_out[6:2]), .PN(4'b0000), .D({cond, iw[27:26], i_dp, iw[24], b_offset[23:22], a_mul, b_offset[20:0]}));
  Add #(.Bits(32)) add_2 (.a(add_1_s), .b(32'h4), .c_i(1'b0), .s(add_2_s));  // open: c_o
  // Probe on {cond, iw[27:26], i_dp, iw[24], b_offset[23:22], a_mul, b_offset[20:0]}
  // Probe on EXT
  // Probe on ALUop
  Multiplexer #(.Bits(32)) multiplexer_3 (.sel(BL), .in_0(out_2), .in_1(add_1_s), .out(multiplexer_3_out));
  Multiplexer #(.Selector_Bits(2), .Bits(4)) multiplexer_4 (
    .sel(ALUop), .in_0(b_offset[3:0]), .in_1(b_offset[3:0]), .in_2(b_offset[11:8]), .in_3(b_offset[3:0]),
    .out(multiplexer_4_out));
  Multiplexer #(.Selector_Bits(2), .Bits(4)) multiplexer_5 (
    .sel(ALUop), .in_0(b_offset[19:16]), .in_1(b_offset[19:16]), .in_2(b_offset[3:0]),
    .in_3(b_offset[19:16]), .out(multiplexer_5_out));
  Multiplexer #(.Selector_Bits(2), .Bits(4)) multiplexer_6 (
    .sel(ALUop), .in_0(b_offset[15:12]), .in_1(b_offset[15:12]), .in_2(b_offset[19:16]),
    .in_3(b_offset[15:12]), .out(multiplexer_6_out));
  // Probe on r0
  // Probe on r1
  // Probe on r2
  // Probe on r3
  // Probe on cond
  // Probe on cond
  // Probe on cond
  // Probe on cond
  Multiplexer #(.Bits(4)) multiplexer_7 (
    .sel(MemWrite), .in_0(multiplexer_4_out), .in_1(b_offset[15:12]), .out(multiplexer_7_out));
  Multiplexer #(.Bits(4)) multiplexer_8 (.sel(BL), .in_0(multiplexer_6_out), .in_1(4'b1110), .out(multiplexer_8_out));
  // Probe on r4
  // Probe on r5
  // Probe on r6
  // Probe on r7
  // Probe on iw[27]
  // Probe on {iw[27:26], i_dp, iw[24], b_offset[23]}
  // Probe on iw[27:26]
  // Probe on i_dp
  // Probe on iw[24]
  Multiplexer #(.Bits(4)) multiplexer_9 (.sel(BR), .in_0(multiplexer_5_out), .in_1(4'b1111), .out(multiplexer_9_out));
  // Probe on r8
  // Probe on r9
  // Probe on r10
  // Probe on r11
  // Probe on i_dp
  // Probe on a_mul
  // Probe on i_dp
  register_file register_file_1 (
    .ReadReg0(multiplexer_9_out), .WriteReg(multiplexer_8_out), .WriteData(multiplexer_3_out), .WriteEn(RFW),
    .CLK(and_1_out), .ReadReg1(multiplexer_7_out), .PC(add_2_s), .RD0(register_file_1_rd0),
    .RD1(register_file_1_rd1), .r0(r0), .r1(r1), .r2(r2), .r3(r3), .r4(r4), .r5(r5), .r6(r6), .r7(r7),
    .r8(r8), .r9(r9), .r10(r10), .r11(r11), .r12(r12), .r13(r13), .r14(r14), .r15(r15));
  // Probe on {iw[24], b_offset[23:22], a_mul}
  // Probe on b_offset[20]
  // Probe on iw[24]
  // Probe on {b_offset[23:22], a_mul, b_offset[20:0]}
  // Probe on b_offset[20]
  // Probe on b_offset[19:16]
  // Probe on b_offset[23]
  // Probe on r12
  // Probe on r13
  // Probe on r14
  // Probe on r15
  // Probe on pc_out
  // Probe on b_offset[19:16]
  // Probe on b_offset[15:12]
  // Probe on b_offset[22]
  extension_unit extension_unit_1 (
    .iw({cond, iw[27:26], i_dp, iw[24], b_offset[23:22], a_mul, b_offset[20:0]}), .EXT(EXT),
    .extimm(extension_unit_1_extimm));
  // Probe on N
  // Probe on Z
  // Probe on C
  // Probe on V
  // Probe on register_file_1_rd0
  // Probe on register_file_1_rd1
  Multiplexer #(.Bits(32)) multiplexer_10 (
    .sel(ALU1src), .in_0(register_file_1_rd1), .in_1(extension_unit_1_extimm), .out(multiplexer_10_out));
  // Probe on b_offset[3:0]
  // Probe on b_offset[11:8]
  // Probe on a_mul
  // Probe on multiplexer_10_out
  // Probe on b_offset[7:0]
  // Probe on b_offset[7:4]
  // Probe on b_offset[20]
  // ALU alu_1: pin names not known; wires that end beside it: register_file_1_rd0, multiplexer_10_out, ALUop, {alu_1_p4_2, alu_1_p4}, NZCV, N, Z, C, V
  // Probe on b_offset[3:0]
  // Probe on b_offset[19:16]
  // Probe on b_offset[15:12]
  // Probe on {alu_1_p4_2, alu_1_p4}
  // Probe on b_offset[3:0]
  Comparator #(.Bits(32)) comparator_1 (.a(pc_in), .b(pc_out), .eq(comparator_1_eq));  // open: gt, lt
  // Probe on b_offset[11:0]
  RAMDualPort #(.AddrBits(9), .Bits(32)) ramdualport_1 (
    .A(alu_1_p4), .Din(register_file_1_rd1), .str(MemWrite), .C(and_1_out), .ld(MemToReg), .D(ramdualport_1_d));
  LED led_1 (.in(comparator_1_eq));
  Multiplexer #(.Bits(32)) multiplexer_11 (
    .sel(MemToReg), .in_0({alu_1_p4_2, alu_1_p4}), .in_1(ramdualport_1_d), .out(out_2));

  // Other names for the same wires on the sheet: imm[7:0] = b_offset[7:0]; immoff[11:0] = b_offset[11:0];
  //   iw (some bits) = {cond, i_dp, b_offset[23:22], a_mul, b_offset[20:0]}; rm[3:0] = b_offset[3:0];
  //   rm_mul[3:0] = b_offset[3:0]; opmul4[3:0] = b_offset[7:4]; rs_mul[3:0] = b_offset[11:8];
  //   rd[3:0] = b_offset[15:12]; rn_mul[3:0] = b_offset[15:12]; rd_mul[3:0] = b_offset[19:16];
  //   rn[3:0] = b_offset[19:16]; l_sdt = b_offset[20]; s_dp = b_offset[20]; s_mul = b_offset[20];
  //   b_offset[21] = a_mul; opc[3:0] = {iw[24], b_offset[23:22], a_mul}; w_sdt = a_mul; b_sdt = b_offset[22];
  //   opmul6[4:0] = {iw[27:26], i_dp, iw[24], b_offset[23]}; u_sdt = b_offset[23]; l_b = iw[24]; p_sdt = iw[24];
  //   i_sdt = i_dp; opb3 = i_dp; op1 = iw[26]; opmul2[1:0] = iw[27:26]; op2 = iw[27]

  // Notes on the sheet:
  //   CLK: Hz: 50
  //   0-1: quadratic ROMs
  //   2-3: sum_array ROMs
  //   4-5: find_max
  //   6: fib_iter(10)
  //   7: fib_iter(19)
  //   8:  fib_rec (10)
  //   9: fib_rec(19)
  //   rm
  //   rd
  //   rn
  //   DP
  //   MUL
  //   SDT
  //   B
  //   SP
  //   LR
  //   PC+8
  //   PC
  //   Finished: RED
endmodule
